# Fritzing sketch WhatToWatch_diagram (saved by Fritzing 0.9.10b)
circuit board: 17.1315cm x 16.0949cm
breadboards: 2

parts:
  M1 = DOIT Esp32 DevKit v1 (30 pins long, 11 pins width) [part_number=ESP32S-PIN30]
  BUTTON1 = Arcade Button (yellow)
  2_8_TFT_SPI_240x320_V1_2 = 2.8 inch LCD SPI display with touch screen & SD card

nets:
  N1: M1.3V3, BUTTON1.no_name_yet#1
  N2: M1.GND, 2_8_TFT_SPI_240x320_V1_2.pin2
  N3: M1.D15, 2_8_TFT_SPI_240x320_V1_2.pin3
  N4: M1.D2, 2_8_TFT_SPI_240x320_V1_2.pin5
  N5: M1.D4, 2_8_TFT_SPI_240x320_V1_2.pin4
  N6: M1.D18, 2_8_TFT_SPI_240x320_V1_2.pin7
  N7: M1.D23, 2_8_TFT_SPI_240x320_V1_2.pin6
  N8: M1.D27, BUTTON1.no_name_yet#2
  N9: 2_8_TFT_SPI_240x320_V1_2.pin1, 2_8_TFT_SPI_240x320_V1_2.pin8

notes:
  VCC
  GND
  CS
  RESET
  DC
  SDI (MOSI)
  SCK
  LED

custom parts:
  DOIT Esp32 DevKit v1 (30 pins long, 11 pins width): The DOIT Esp32 DevKit v1 is one of the development board created by DOIT to evaluate the ESP-WROOM-32 module. It is based on the ESP32 microcontroller that boasts Wifi, Bluetooth, Ethernet and Low Power support all in a single chip. (vanepp) made breadboard work, adjusted pin numbering and labels and reduced size of schematic and cleaned up pcb. This chip is 30pins long (2 x15) and 11 pins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
  Arcade Button (yellow): Adafruit Arcade Button (yellow)
  2.8 inch LCD SPI display with touch screen & SD card: A generic 2.8 inch LCD TFT 320x280 display with touchscreen and SD card slot.
